# Fritzing sketch Circuit_Components (saved by Fritzing 0.9.6b)
breadboards: 1

parts:
  Gizwits_WiFi_Witty_ESP-12F1 = Gizwits WiFi Witty ESP-12F
  DHT1 = DHT11 Humitidy and Temperature Sensor

nets:
  VCC: Gizwits_WiFi_Witty_ESP-12F1.VCC, DHT1.VDD
  GND: Gizwits_WiFi_Witty_ESP-12F1.GND, DHT1.GND
  N1: Gizwits_WiFi_Witty_ESP-12F1.GPIO5, DHT1.DATA

custom parts:
  DHT11 Humitidy and Temperature Sensor: DHT11 Humidity and Temperature Sensor
